// Logisim project snatch game.circ as structural Verilog: 1 circuit, main circuit main
module main (
);

  wire ACERTADO_0, ACERTADO_1, ACERTADO_2, ACERTADO_3, ACERTADO_4, ACERTADO_5, ACERTADO_6, ACERTADO_7,
       ACERTADO_8, ACERTADO_9, ACERTADO_A, ACERTADO_B, ACERTADO_C, ACERTADO_D, ACERTADO_E, ACERTADO_F,
       and_21_out, and_22_out, and_23_out, and_24_out, and_25_out, and_26_out, and_27_out, and_28_out,
       and_29_out, and_30_out, and_31_out, and_32_out, and_33_out, and_34_out, and_35_out, and_36_out,
       and_37_out, and_38_out, and_39_out, and_40_out, and_41_out, and_42_out, and_43_out, and_44_out,
       and_45_out, and_46_out, and_47_out, and_48_out, and_49_out, and_50_out, and_51_out, and_52_out,
       and_69_out, and_70_out, and_72_out, and_73_out, and_75_out, and_76_out, and_77_out, and_78_out,
       and_79_out, and_80_out, and_81_out, and_82_out, and_83_out, and_84_out, and_85_out, and_86_out,
       and_87_out, and_88_out, and_89_out, and_90_out, and_91_out, and_92_out, and_93_out, and_94_out,
       and_95_out, and_96_out, and_97_out, and_98_out, and_99_out, and_100_out, and_101_out, and_102_out,
       and_103_out, and_104_out, and_105_out, and_106_out, and_107_out, and_108_out, and_109_out,
       and_110_out, and_111_out, and_112_out, and_113_out, and_114_out, and_115_out, and_116_out,
       and_117_out, and_118_out, and_119_out, and_120_out, and_121_out, and_122_out, and_123_out,
       and_124_out, and_125_out, and_126_out, and_127_out, and_128_out, and_129_out, and_130_out,
       and_131_out, and_132_out, and_133_out, and_134_out, and_135_out, and_136_out, and_137_out,
       and_138_out, BOTAO_COLUNA, BOTAO_LINHA, CHECK, comparator_1_eq, comparator_2_eq, CONFIRMA,
       counter_7_q, counter_8_q, counter_9_q, counter_10_q, counter_11_q, counter_12_q, counter_13_q,
       counter_14_q, counter_15_q, counter_16_q, counter_17_q, counter_18_q, counter_19_q, counter_20_q,
       counter_21_q, counter_22_q, ESTADO_0, ESTADO_1, ESTADO_2, ESTADO_3, IGUALDADE, JOGADOR0, JOGADOR1, L0,
       L1, L2, L3, L4, L5, L6, L7, L8, L9, LA, LB, LC, LD, LE, LF, MUX0, MUX1, MUX2, MUX3, MUX4, MUX5, MUX6,
       MUX7, MUX8, MUX9, MUXA, MUXB, MUXC, MUXD, MUXE, MUXF, or_1_out, or_2_out, or_3_out, or_4_out,
       or_5_out, or_6_out, or_7_out, or_8_out, or_9_out, or_10_out, or_11_out, or_12_out, or_13_out,
       or_14_out, or_15_out, or_16_out;
  wire [1:0] COLUNA, COLUNA_1, COLUNA_2, counter_4_q, LINHA, LINHA_1, LINHA_2;
  wire [3:0] multiplexer_1_out, multiplexer_2_out, PONTUACAO0, PONTUACAO1, V0, V1, V2, V3, V4, V5, V6, V7,
       V8, V9, VA, VB, VC, VD, VE, VF;

  Counter #(.width(1), .max('h1)) counter_1 (.Q(JOGADOR1), .clk(ESTADO_0));  // open: load, D, count, carry, clr
  Counter #(.width(2), .max('h3)) counter_2 (.Q(COLUNA), .clk(BOTAO_COLUNA));  // open: load, D, count, carry, clr
  Counter #(.width(2), .max('h3)) counter_3 (.Q(LINHA), .clk(BOTAO_LINHA));  // open: load, D, count, carry, clr
  and and_1 (L0, ~LINHA[1], ~LINHA[0], ~COLUNA[1], ~COLUNA[0]);  // AND_Gate
  and and_2 (L1, ~LINHA[1], ~LINHA[0], ~COLUNA[1], COLUNA[0]);  // AND_Gate
  and and_3 (L2, ~LINHA[1], ~LINHA[0], COLUNA[1], ~COLUNA[0]);  // AND_Gate
  and and_4 (L3, ~LINHA[1], ~LINHA[0], COLUNA[1], COLUNA[0]);  // AND_Gate
  and and_5 (L4, ~LINHA[1], LINHA[0], ~COLUNA[1], ~COLUNA[0]);  // AND_Gate
  and and_6 (L5, ~LINHA[1], LINHA[0], ~COLUNA[1], COLUNA[0]);  // AND_Gate
  and and_7 (L6, ~LINHA[1], LINHA[0], COLUNA[1], ~COLUNA[0]);  // AND_Gate
  and and_8 (L7, ~LINHA[1], LINHA[0], COLUNA[1], COLUNA[0]);  // AND_Gate
  and and_9 (L8, LINHA[1], ~LINHA[0], ~COLUNA[1], ~COLUNA[0]);  // AND_Gate
  and and_10 (L9, LINHA[1], ~LINHA[0], ~COLUNA[1], COLUNA[0]);  // AND_Gate
  and and_11 (LA, LINHA[1], ~LINHA[0], COLUNA[1], ~COLUNA[0]);  // AND_Gate
  and and_12 (LB, LINHA[1], ~LINHA[0], COLUNA[1], COLUNA[0]);  // AND_Gate
  and and_13 (LC, LINHA[1], LINHA[0], ~COLUNA[1], ~COLUNA[0]);  // AND_Gate
  and and_14 (LD, LINHA[1], LINHA[0], ~COLUNA[1], COLUNA[0]);  // AND_Gate
  and and_15 (LE, LINHA[1], LINHA[0], COLUNA[1], ~COLUNA[0]);  // AND_Gate
  and and_16 (LF, LINHA[1], LINHA[0], COLUNA[1], COLUNA[0]);
  not not_1 (JOGADOR0, JOGADOR1);
  Hex_Digit_Display hex_digit_display_1 (.value(PONTUACAO0));  // open: dp
  LED Jogador_0 (.in(JOGADOR0));
  LED Jogador_1 (.in(JOGADOR1));
  LED led_1 (.in(L0));
  Hex_Digit_Display hex_digit_display_2 (.value(V0));  // open: dp
  LED led_2 (.in(L4));
  Hex_Digit_Display hex_digit_display_3 (.value(V4));  // open: dp
  LED led_3 (.in(L8));
  Hex_Digit_Display hex_digit_display_4 (.value(V8));  // open: dp
  LED led_4 (.in(LC));
  Hex_Digit_Display hex_digit_display_5 (.value(VC));  // open: dp
  Counter #(.width(2), .max('h3)) counter_4 (
    .load(IGUALDADE), .count(1'b1), .Q(counter_4_q), .clk(CONFIRMA), .clr(ESTADO_3));  // open: D, carry
  Button button_1 (.out(BOTAO_LINHA));
  and and_17 (ESTADO_0, ~counter_4_q[0], ~counter_4_q[1]);  // AND_Gate
  and and_18 (ESTADO_1, counter_4_q[0], ~counter_4_q[1]);  // AND_Gate
  and and_19 (ESTADO_2, ~counter_4_q[0], counter_4_q[1]);  // AND_Gate
  and and_20 (ESTADO_3, counter_4_q[0], counter_4_q[1]);
  and and_21 (and_21_out, ~LINHA_1[1], ~LINHA_1[0], ~COLUNA_1[1], COLUNA_1[0]);  // AND_Gate
  and and_22 (and_22_out, ~LINHA_2[1], ~LINHA_2[0], ~COLUNA_2[1], COLUNA_2[0]);  // AND_Gate
  and and_23 (and_23_out, ~LINHA_1[1], ~LINHA_1[0], COLUNA_1[1], ~COLUNA_1[0]);  // AND_Gate
  and and_24 (and_24_out, ~LINHA_2[1], ~LINHA_2[0], COLUNA_2[1], ~COLUNA_2[0]);  // AND_Gate
  and and_25 (and_25_out, ~LINHA_1[1], ~LINHA_1[0], COLUNA_1[1], COLUNA_1[0]);  // AND_Gate
  and and_26 (and_26_out, ~LINHA_2[1], ~LINHA_2[0], COLUNA_2[1], COLUNA_2[0]);  // AND_Gate
  and and_27 (and_27_out, ~LINHA_1[1], LINHA_1[0], ~COLUNA_1[1], ~COLUNA_1[0]);  // AND_Gate
  and and_28 (and_28_out, ~LINHA_1[1], LINHA_1[0], ~COLUNA_1[1], COLUNA_1[0]);  // AND_Gate
  LED led_5 (.in(L1));
  Hex_Digit_Display hex_digit_display_6 (.value(V1));  // open: dp
  LED led_6 (.in(L5));
  Hex_Digit_Display hex_digit_display_7 (.value(V5));  // open: dp
  LED led_7 (.in(L9));
  Hex_Digit_Display hex_digit_display_8 (.value(V9));  // open: dp
  LED led_8 (.in(LD));
  Hex_Digit_Display hex_digit_display_9 (.value(VD));  // open: dp
  and and_29 (and_29_out, ~LINHA_1[1], ~LINHA_1[0], ~COLUNA_1[1], ~COLUNA_1[0]);  // AND_Gate
  and and_30 (and_30_out, ~LINHA_2[1], ~LINHA_2[0], ~COLUNA_2[1], ~COLUNA_2[0]);  // AND_Gate
  and and_31 (and_31_out, ~LINHA_1[1], LINHA_1[0], ~COLUNA_1[1], ~COLUNA_1[0]);  // AND_Gate
  and and_32 (and_32_out, ~LINHA_2[1], LINHA_2[0], ~COLUNA_2[1], COLUNA_2[0]);  // AND_Gate
  and and_33 (and_33_out, ~LINHA_1[1], LINHA_1[0], COLUNA_1[1], ~COLUNA_1[0]);  // AND_Gate
  and and_34 (and_34_out, ~LINHA_2[1], LINHA_2[0], COLUNA_2[1], ~COLUNA_2[0]);  // AND_Gate
  and and_35 (and_35_out, ~LINHA_1[1], LINHA_1[0], COLUNA_1[1], COLUNA_1[0]);  // AND_Gate
  and and_36 (and_36_out, ~LINHA_2[1], LINHA_2[0], COLUNA_2[1], COLUNA_2[0]);  // AND_Gate
  and and_37 (and_37_out, LINHA_1[1], ~LINHA_1[0], ~COLUNA_1[1], ~COLUNA_1[0]);  // AND_Gate
  and and_38 (and_38_out, LINHA_2[1], ~LINHA_2[0], ~COLUNA_2[1], ~COLUNA_2[0]);  // AND_Gate
  and and_39 (and_39_out, LINHA_1[1], ~LINHA_1[0], ~COLUNA_1[1], COLUNA_1[0]);  // AND_Gate
  and and_40 (and_40_out, LINHA_2[1], ~LINHA_2[0], ~COLUNA_2[1], COLUNA_2[0]);  // AND_Gate
  and and_41 (and_41_out, LINHA_1[1], ~LINHA_1[0], COLUNA_1[1], ~COLUNA_1[0]);  // AND_Gate
  and and_42 (and_42_out, LINHA_2[1], ~LINHA_2[0], COLUNA_2[1], ~COLUNA_2[0]);  // AND_Gate
  and and_43 (and_43_out, LINHA_1[1], ~LINHA_1[0], COLUNA_1[1], COLUNA_1[0]);  // AND_Gate
  and and_44 (and_44_out, LINHA_2[1], ~LINHA_2[0], COLUNA_2[1], COLUNA_2[0]);  // AND_Gate
  and and_45 (and_45_out, LINHA_1[1], LINHA_1[0], ~COLUNA_1[1], ~COLUNA_1[0]);  // AND_Gate
  and and_46 (and_46_out, LINHA_2[1], LINHA_2[0], ~COLUNA_2[1], ~COLUNA_2[0]);  // AND_Gate
  and and_47 (and_47_out, LINHA_1[1], LINHA_1[0], ~COLUNA_1[1], COLUNA_1[0]);  // AND_Gate
  and and_48 (and_48_out, LINHA_2[1], LINHA_2[0], ~COLUNA_2[1], COLUNA_2[0]);  // AND_Gate
  and and_49 (and_49_out, LINHA_1[1], LINHA_1[0], COLUNA_1[1], ~COLUNA_1[0]);  // AND_Gate
  and and_50 (and_50_out, LINHA_2[1], LINHA_2[0], COLUNA_2[1], ~COLUNA_2[0]);  // AND_Gate
  and and_51 (and_51_out, LINHA_1[1], LINHA_1[0], COLUNA_1[1], COLUNA_1[0]);
  and and_52 (and_52_out, LINHA_2[1], LINHA_2[0], COLUNA_2[1], COLUNA_2[0]);
  Button button_2 (.out(CONFIRMA));
  or or_1 (or_1_out, and_29_out, and_30_out);
  or or_2 (or_2_out, and_21_out, and_22_out);
  or or_3 (or_3_out, and_23_out, and_24_out);
  or or_4 (or_4_out, and_25_out, and_26_out);
  or or_5 (or_5_out, and_27_out, and_31_out);
  or or_6 (or_6_out, and_28_out, and_32_out);
  or or_7 (or_7_out, and_33_out, and_34_out);
  or or_8 (or_8_out, and_35_out, and_36_out);
  or or_9 (or_9_out, and_37_out, and_38_out);
  or or_10 (or_10_out, and_39_out, and_40_out);
  or or_11 (or_11_out, and_41_out, and_42_out);
  or or_12 (or_12_out, and_43_out, and_44_out);
  or or_13 (or_13_out, and_45_out, and_46_out);
  or or_14 (or_14_out, and_47_out, and_48_out);
  or or_15 (or_15_out, and_49_out, and_50_out);
  or or_16 (or_16_out, and_51_out, and_52_out);
  LED led_9 (.in(L2));
  Hex_Digit_Display hex_digit_display_10 (.value(V2));  // open: dp
  LED led_10 (.in(L6));
  Hex_Digit_Display hex_digit_display_11 (.value(V6));  // open: dp
  LED led_11 (.in(LA));
  Hex_Digit_Display hex_digit_display_12 (.value(VA));  // open: dp
  LED led_12 (.in(LE));
  Hex_Digit_Display hex_digit_display_13 (.value(VE));  // open: dp
  and and_53 (ACERTADO_0, CHECK, or_1_out);
  and and_54 (ACERTADO_1, CHECK, or_2_out);
  and and_55 (ACERTADO_2, CHECK, or_3_out);
  and and_56 (ACERTADO_3, CHECK, or_4_out);
  and and_57 (ACERTADO_4, CHECK, or_5_out);
  and and_58 (ACERTADO_5, CHECK, or_6_out);
  and and_59 (ACERTADO_6, CHECK, or_7_out);
  and and_60 (ACERTADO_7, CHECK, or_8_out);
  and and_61 (ACERTADO_8, CHECK, or_9_out);
  and and_62 (ACERTADO_9, CHECK, or_10_out);
  and and_63 (ACERTADO_A, CHECK, or_11_out);
  and and_64 (ACERTADO_B, CHECK, or_12_out);
  and and_65 (ACERTADO_C, CHECK, or_13_out);
  and and_66 (ACERTADO_D, CHECK, or_14_out);
  and and_67 (ACERTADO_E, CHECK, or_15_out);
  and and_68 (ACERTADO_F, CHECK, or_16_out);
  Button button_3 (.out(BOTAO_COLUNA));
  Register #(.width(2)) register_1 (.D(LINHA), .Q(LINHA_1), .clk(and_69_out));  // open: en, clr
  Register #(.width(2)) register_2 (.D(COLUNA), .Q(COLUNA_1), .clk(and_69_out));  // open: en, clr
  and and_69 (and_69_out, CONFIRMA, ESTADO_0);
  Hex_Digit_Display hex_digit_display_14 (.value(PONTUACAO1));  // open: dp
  LED led_13 (.in(L3));
  Hex_Digit_Display hex_digit_display_15 (.value(V3));  // open: dp
  LED led_14 (.in(L7));
  Hex_Digit_Display hex_digit_display_16 (.value(V7));  // open: dp
  LED led_15 (.in(LB));
  Hex_Digit_Display hex_digit_display_17 (.value(VB));  // open: dp
  LED led_16 (.in(LF));
  Hex_Digit_Display hex_digit_display_18 (.value(VF));  // open: dp
  Register #(.width(2)) register_3 (.D(LINHA), .Q(LINHA_2), .clk(and_70_out), .clr(ESTADO_0));  // open: en
  Register #(.width(2)) register_4 (.D(COLUNA), .Q(COLUNA_2), .clk(and_70_out), .clr(ESTADO_0));  // open: en
  and and_70 (and_70_out, CONFIRMA, ESTADO_1);
  Multiplexer #(.select(4), .width(4)) multiplexer_1 (
    .in0(4'b1111), .in1(4'b0010), .in2(4'b1100), .in3(4'b0100), .in4(4'b1011), .in5(4'b1010), .in6(4'b1111),
    .in7(4'b1101), .in8(4'b1010), .in9(4'b1110), .in10(4'b1100), .in11(4'b1110), .in12(4'b1011),
    .in13(4'b0010), .in14(4'b0100), .in15(4'b1101), .out(multiplexer_1_out), .sel({LINHA_1, COLUNA_1}));  // open: en
  Multiplexer #(.select(4), .width(4)) multiplexer_2 (
    .in0(4'b1111), .in1(4'b0010), .in2(4'b1100), .in3(4'b0100), .in4(4'b1011), .in5(4'b1010), .in6(4'b1111),
    .in7(4'b1101), .in8(4'b1010), .in9(4'b1110), .in10(4'b1100), .in11(4'b1110), .in12(4'b1011),
    .in13(4'b0010), .in14(4'b0100), .in15(4'b1101), .out(multiplexer_2_out), .sel({LINHA_2, COLUNA_2}));  // open: en
  Comparator #(.width(4)) comparator_1 (
    .a(multiplexer_1_out), .b(multiplexer_2_out), .eq(comparator_1_eq));  // open: gt, lt
  and and_71 (CHECK, comparator_1_eq, ESTADO_3);
  Multiplexer #(.width(4)) multiplexer_3 (.in1(4'b1111), .out(V0), .sel(MUX0));  // open: in0, en
  Multiplexer #(.width(4)) multiplexer_4 (.in1(4'b1100), .out(V2), .sel(MUX2));  // open: in0, en
  Multiplexer #(.width(4)) multiplexer_5 (.in1(4'b1011), .out(V4), .sel(MUX4));  // open: in0, en
  Multiplexer #(.width(4)) multiplexer_6 (.in1(4'b1111), .out(V6), .sel(MUX6));  // open: in0, en
  Multiplexer #(.width(4)) multiplexer_7 (.in1(4'b1010), .out(V8), .sel(MUX8));  // open: in0, en
  Multiplexer #(.width(4)) multiplexer_8 (.in1(4'b1100), .out(VA), .sel(MUXA));  // open: in0, en
  Multiplexer #(.width(4)) multiplexer_9 (.in1(4'b1011), .out(VC), .sel(MUXC));  // open: in0, en
  Multiplexer #(.width(4)) multiplexer_10 (.in1(4'b0100), .out(VE), .sel(MUXE));  // open: in0, en
  Comparator #(.width(4)) comparator_2 (
    .a({LINHA_1, COLUNA_1}), .b({LINHA_2, COLUNA_2}), .eq(comparator_2_eq));  // open: gt, lt
  Counter #(.width(4), .max('hf)) counter_5 (.Q(PONTUACAO0), .clk(and_72_out));  // open: load, D, count, carry, clr
  and and_72 (and_72_out, CHECK, JOGADOR0);
  Counter #(.width(4), .max('hf)) counter_6 (.Q(PONTUACAO1), .clk(and_73_out));  // open: load, D, count, carry, clr
  and and_73 (and_73_out, CHECK, JOGADOR1);
  and and_74 (IGUALDADE, comparator_2_eq, ESTADO_2);
  Multiplexer #(.width(4)) multiplexer_11 (.in1(4'b0010), .out(V1), .sel(MUX1));  // open: in0, en
  Multiplexer #(.width(4)) multiplexer_12 (.in1(4'b0100), .out(V3), .sel(MUX3));  // open: in0, en
  Multiplexer #(.width(4)) multiplexer_13 (.in1(4'b1010), .out(V5), .sel(MUX5));  // open: in0, en
  Multiplexer #(.width(4)) multiplexer_14 (.in1(4'b1101), .out(V7), .sel(MUX7));  // open: in0, en
  Multiplexer #(.width(4)) multiplexer_15 (.in1(4'b1110), .out(V9), .sel(MUX9));  // open: in0, en
  Multiplexer #(.width(4)) multiplexer_16 (.in1(4'b1110), .out(VB), .sel(MUXB));  // open: in0, en
  Multiplexer #(.width(4)) multiplexer_17 (.in1(4'b0010), .out(VD), .sel(MUXD));  // open: in0, en
  Multiplexer #(.width(4)) multiplexer_18 (.in1(4'b1101), .out(VF), .sel(MUXF));  // open: in0, en
  and and_75 (and_75_out, ~LINHA_1[1], ~LINHA_1[0], ~COLUNA_1[1], ~COLUNA_1[0]);  // AND_Gate
  and and_76 (and_76_out, ~LINHA_2[1], ~LINHA_2[0], ~COLUNA_2[1], ~COLUNA_2[0]);  // AND_Gate
  and and_77 (and_77_out, ~LINHA_1[1], ~LINHA_1[0], ~COLUNA_1[1], COLUNA_1[0]);  // AND_Gate
  and and_78 (and_78_out, ~LINHA_2[1], ~LINHA_2[0], ~COLUNA_2[1], COLUNA_2[0]);  // AND_Gate
  and and_79 (and_79_out, ~LINHA_1[1], ~LINHA_1[0], COLUNA_1[1], ~COLUNA_1[0]);  // AND_Gate
  and and_80 (and_80_out, ~LINHA_2[1], ~LINHA_2[0], COLUNA_2[1], ~COLUNA_2[0]);  // AND_Gate
  and and_81 (and_81_out, ~LINHA_1[1], ~LINHA_1[0], COLUNA_1[1], COLUNA_1[0]);  // AND_Gate
  and and_82 (and_82_out, ~LINHA_2[1], ~LINHA_2[0], COLUNA_2[1], COLUNA_2[0]);  // AND_Gate
  and and_83 (and_83_out, ~LINHA_1[1], LINHA_1[0], ~COLUNA_1[1], ~COLUNA_1[0]);  // AND_Gate
  and and_84 (and_84_out, ~LINHA_1[1], LINHA_1[0], ~COLUNA_1[1], ~COLUNA_1[0]);  // AND_Gate
  and and_85 (and_85_out, ~LINHA_1[1], LINHA_1[0], ~COLUNA_1[1], COLUNA_1[0]);  // AND_Gate
  and and_86 (and_86_out, ~LINHA_2[1], LINHA_2[0], ~COLUNA_2[1], COLUNA_2[0]);  // AND_Gate
  and and_87 (and_87_out, ~LINHA_1[1], LINHA_1[0], COLUNA_1[1], ~COLUNA_1[0]);  // AND_Gate
  and and_88 (and_88_out, ~LINHA_2[1], LINHA_2[0], COLUNA_2[1], ~COLUNA_2[0]);  // AND_Gate
  and and_89 (and_89_out, ~LINHA_1[1], LINHA_1[0], COLUNA_1[1], COLUNA_1[0]);  // AND_Gate
  and and_90 (and_90_out, ~LINHA_2[1], LINHA_2[0], COLUNA_2[1], COLUNA_2[0]);  // AND_Gate
  and and_91 (and_91_out, LINHA_1[1], ~LINHA_1[0], ~COLUNA_1[1], ~COLUNA_1[0]);  // AND_Gate
  and and_92 (and_92_out, LINHA_2[1], ~LINHA_2[0], ~COLUNA_2[1], ~COLUNA_2[0]);  // AND_Gate
  and and_93 (and_93_out, LINHA_1[1], ~LINHA_1[0], ~COLUNA_1[1], COLUNA_1[0]);  // AND_Gate
  and and_94 (and_94_out, LINHA_2[1], ~LINHA_2[0], ~COLUNA_2[1], COLUNA_2[0]);  // AND_Gate
  and and_95 (and_95_out, LINHA_1[1], ~LINHA_1[0], COLUNA_1[1], ~COLUNA_1[0]);  // AND_Gate
  and and_96 (and_96_out, LINHA_2[1], ~LINHA_2[0], COLUNA_2[1], ~COLUNA_2[0]);  // AND_Gate
  and and_97 (and_97_out, LINHA_1[1], ~LINHA_1[0], COLUNA_1[1], COLUNA_1[0]);  // AND_Gate
  and and_98 (and_98_out, LINHA_2[1], ~LINHA_2[0], COLUNA_2[1], COLUNA_2[0]);  // AND_Gate
  and and_99 (and_99_out, LINHA_1[1], LINHA_1[0], ~COLUNA_1[1], ~COLUNA_1[0]);  // AND_Gate
  and and_100 (and_100_out, LINHA_2[1], LINHA_2[0], ~COLUNA_2[1], ~COLUNA_2[0]);  // AND_Gate
  and and_101 (and_101_out, LINHA_1[1], LINHA_1[0], ~COLUNA_1[1], COLUNA_1[0]);  // AND_Gate
  and and_102 (and_102_out, LINHA_2[1], LINHA_2[0], ~COLUNA_2[1], COLUNA_2[0]);  // AND_Gate
  and and_103 (and_103_out, LINHA_1[1], LINHA_1[0], COLUNA_1[1], ~COLUNA_1[0]);  // AND_Gate
  and and_104 (and_104_out, LINHA_2[1], LINHA_2[0], COLUNA_2[1], ~COLUNA_2[0]);  // AND_Gate
  and and_105 (and_105_out, LINHA_1[1], LINHA_1[0], COLUNA_1[1], COLUNA_1[0]);
  and and_106 (and_106_out, LINHA_2[1], LINHA_2[0], COLUNA_2[1], COLUNA_2[0]);
  and and_107 (and_107_out, ESTADO_2, and_85_out);
  and and_108 (and_108_out, ~ESTADO_0, and_86_out);  // AND_Gate
  and and_109 (and_109_out, ESTADO_2, and_75_out);
  and and_110 (and_110_out, ~ESTADO_0, and_76_out);  // AND_Gate
  Counter #(.width(1), .max('h1)) counter_7 (.Q(counter_7_q), .clk(ACERTADO_0));  // open: load, D, count, carry, clr
  and and_111 (and_111_out, ESTADO_2, and_77_out);
  and and_112 (and_112_out, ~ESTADO_0, and_78_out);  // AND_Gate
  Counter #(.width(1), .max('h1)) counter_8 (.Q(counter_8_q), .clk(ACERTADO_1));  // open: load, D, count, carry, clr
  and and_113 (and_113_out, ESTADO_2, and_79_out);
  and and_114 (and_114_out, ~ESTADO_0, and_80_out);  // AND_Gate
  Counter #(.width(1), .max('h1)) counter_9 (.Q(counter_9_q), .clk(ACERTADO_2));  // open: load, D, count, carry, clr
  and and_115 (and_115_out, ESTADO_2, and_81_out);
  and and_116 (and_116_out, ~ESTADO_0, and_82_out);  // AND_Gate
  Counter #(.width(1), .max('h1)) counter_10 (.Q(counter_10_q), .clk(ACERTADO_3));  // open: load, D, count, carry, clr
  and and_117 (and_117_out, ESTADO_2, and_83_out);
  and and_118 (and_118_out, ~ESTADO_0, and_84_out);  // AND_Gate
  Counter #(.width(1), .max('h1)) counter_11 (.Q(counter_11_q), .clk(ACERTADO_4));  // open: load, D, count, carry, clr
  Counter #(.width(1), .max('h1)) counter_12 (.Q(counter_12_q), .clk(ACERTADO_5));  // open: load, D, count, carry, clr
  and and_119 (and_119_out, ESTADO_2, and_87_out);
  and and_120 (and_120_out, ~ESTADO_0, and_88_out);  // AND_Gate
  Counter #(.width(1), .max('h1)) counter_13 (.Q(counter_13_q), .clk(ACERTADO_6));  // open: load, D, count, carry, clr
  and and_121 (and_121_out, ESTADO_2, and_89_out);
  and and_122 (and_122_out, ~ESTADO_0, and_90_out);  // AND_Gate
  Counter #(.width(1), .max('h1)) counter_14 (.Q(counter_14_q), .clk(ACERTADO_7));  // open: load, D, count, carry, clr
  and and_123 (and_123_out, ESTADO_2, and_91_out);
  and and_124 (and_124_out, ~ESTADO_0, and_92_out);  // AND_Gate
  Counter #(.width(1), .max('h1)) counter_15 (.Q(counter_15_q), .clk(ACERTADO_8));  // open: load, D, count, carry, clr
  and and_125 (and_125_out, ESTADO_2, and_93_out);
  and and_126 (and_126_out, ~ESTADO_0, and_94_out);  // AND_Gate
  Counter #(.width(1), .max('h1)) counter_16 (.Q(counter_16_q), .clk(ACERTADO_9));  // open: load, D, count, carry, clr
  and and_127 (and_127_out, ESTADO_2, and_95_out);
  and and_128 (and_128_out, ~ESTADO_0, and_96_out);  // AND_Gate
  Counter #(.width(1), .max('h1)) counter_17 (.Q(counter_17_q), .clk(ACERTADO_A));  // open: load, D, count, carry, clr
  and and_129 (and_129_out, ESTADO_2, and_97_out);
  and and_130 (and_130_out, ~ESTADO_0, and_98_out);  // AND_Gate
  Counter #(.width(1), .max('h1)) counter_18 (.Q(counter_18_q), .clk(ACERTADO_B));  // open: load, D, count, carry, clr
  and and_131 (and_131_out, ESTADO_2, and_99_out);
  and and_132 (and_132_out, ~ESTADO_0, and_100_out);  // AND_Gate
  Counter #(.width(1), .max('h1)) counter_19 (.Q(counter_19_q), .clk(ACERTADO_C));  // open: load, D, count, carry, clr
  and and_133 (and_133_out, ESTADO_2, and_101_out);
  and and_134 (and_134_out, ~ESTADO_0, and_102_out);  // AND_Gate
  Counter #(.width(1), .max('h1)) counter_20 (.Q(counter_20_q), .clk(ACERTADO_D));  // open: load, D, count, carry, clr
  and and_135 (and_135_out, ESTADO_2, and_103_out);
  and and_136 (and_136_out, ~ESTADO_0, and_104_out);  // AND_Gate
  Counter #(.width(1), .max('h1)) counter_21 (.Q(counter_21_q), .clk(ACERTADO_E));  // open: load, D, count, carry, clr
  and and_137 (and_137_out, ESTADO_2, and_105_out);
  and and_138 (and_138_out, ~ESTADO_0, and_106_out);  // AND_Gate
  Counter #(.width(1), .max('h1)) counter_22 (.Q(counter_22_q), .clk(ACERTADO_F));  // open: load, D, count, carry, clr
  or or_17 (MUX1, and_111_out, and_112_out, counter_8_q);
  or or_18 (MUX4, and_117_out, and_118_out, counter_11_q);
  or or_19 (MUX5, and_107_out, and_108_out, counter_12_q);
  or or_20 (MUX6, and_119_out, and_120_out, counter_13_q);
  or or_21 (MUX0, and_109_out, and_110_out, counter_7_q);
  or or_22 (MUX2, and_113_out, and_114_out, counter_9_q);
  or or_23 (MUX3, and_115_out, and_116_out, counter_10_q);
  or or_24 (MUX7, and_121_out, and_122_out, counter_14_q);
  or or_25 (MUX8, and_123_out, and_124_out, counter_15_q);
  or or_26 (MUX9, and_125_out, and_126_out, counter_16_q);
  or or_27 (MUXA, and_127_out, and_128_out, counter_17_q);
  or or_28 (MUXB, and_129_out, and_130_out, counter_18_q);
  or or_29 (MUXC, and_131_out, and_132_out, counter_19_q);
  or or_30 (MUXD, and_133_out, and_134_out, counter_20_q);
  or or_31 (MUXE, and_135_out, and_136_out, counter_21_q);
  or or_32 (MUXF, and_137_out, and_138_out, counter_22_q);
endmodule
